# Fritzing sketch wireing (saved by Fritzing 0.9.3b)
circuit board: 18.3727cm x 12.7282cm
breadboards: 3

parts:
  S1 = Round Pushbutton
  S2 = Round Pushbutton
  LED1 = LED - 5mm [color="Red (633nm)" package="5 mm [THT]"]
  LED2 = LED - 5mm [color="Red (633nm)" package="5 mm [THT]"]
  LED3 = LED - 5mm [color="Red (633nm)" package="5 mm [THT]"]
  LED4 = LED - 5mm [color="Red (633nm)" package="5 mm [THT]"]
  7_Segment1 = 7 Segment Display
  7_Segment2 = 7 Segment Display
  Power_plug1 = Power plug
  Q1 = PNP-Transistor [package="TO92 [THT]"]
  Q2 = PNP-Transistor [package="TO92 [THT]"]
  Q3 = PNP-Transistor [package="TO92 [THT]"]
  Q5 = PNP-Transistor [package="TO92 [THT]"]
  Q6 = PNP-Transistor [package="TO92 [THT]"]
  Q8 = PNP-Transistor [package="TO92 [THT]"]
  Part1 = Arduino Mega 2560 (Rev3)
  R9 = Resistor [tolerance=±5% resistance=1k package=THT]
  R10 = Resistor [tolerance=±5% resistance=1k package=THT]
  R11 = Resistor [tolerance=±5% resistance=1k package=THT]
  Q4 = PNP-Transistor [package="TO92 [THT]"]
  R12 = Resistor [tolerance=±5% resistance=1k package=THT]
  R13 = Resistor [tolerance=±5% resistance=1k package=THT]
  R14 = Resistor [tolerance=±5% resistance=1k package=THT]
  R15 = Resistor [tolerance=±5% resistance=1k package=THT]
  Q9 = PNP-Transistor [package="TO92 [THT]"]
  Q10 = PNP-Transistor [package="TO92 [THT]"]
  Q11 = PNP-Transistor [package="TO92 [THT]"]
  Q12 = PNP-Transistor [package="TO92 [THT]"]
  Q13 = PNP-Transistor [package="TO92 [THT]"]
  Q14 = PNP-Transistor [package="TO92 [THT]"]
  Q15 = PNP-Transistor [package="TO92 [THT]"]
  R16 = Resistor [tolerance=±5% resistance=22 package=THT]
  R17 = Resistor [tolerance=±5% resistance=22 package=THT]
  R18 = Resistor [tolerance=±5% resistance=22 package=THT]
  R19 = Resistor [tolerance=±5% resistance=22 package=THT]
  R20 = Resistor [tolerance=±5% resistance=22 package=THT]
  R21 = Resistor [tolerance=±5% resistance=22 package=THT]
  R22 = Resistor [tolerance=±5% resistance=22 package=THT]
  R23 = Resistor [tolerance=±5% resistance=1k package=THT]
  R24 = Resistor [tolerance=±5% resistance=1k package=THT]
  R25 = Resistor [tolerance=±5% resistance=1k package=THT]
  R26 = Resistor [tolerance=±5% resistance=1k package=THT]
  R27 = Resistor [tolerance=±5% resistance=1k package=THT]
  R28 = Resistor [tolerance=±5% resistance=1k package=THT]
  R29 = Resistor [tolerance=±5% resistance=1k package=THT]
  Part2 = RFID-RC522-v3
  Part3 = RFID-RC522-v3
  Part4 = RFID-RC522-v3
  Part5 = RFID-RC522-v3
  R30 = Resistor [tolerance=±5% resistance=10k package=THT]
  R31 = Resistor [tolerance=±5% resistance=10k package=THT]
  R32 = Resistor [tolerance=±5% resistance=220 package=THT]
  R33 = Resistor [tolerance=±5% resistance=220 package=THT]
  R34 = Resistor [tolerance=±5% resistance=220 package=THT]
  R35 = Resistor [tolerance=±5% resistance=220 package=THT]

nets (from the breadboard view):
  N1: S1.leg0, Part1.D37, R31.Pin_1
  3.3V: S1.leg1, S2.leg1, Part1.5V, Part2.3.3V, Part3.3.3V, Part4.3.3V, Part5.3.3V
  N2: S2.leg0, Part1.D36, R30.Pin_1
  N3: LED1.cathode, R35.Pin_0
  GND: LED1.anode, LED2.anode, LED3.anode, LED4.anode, Power_plug1.GND, Q1.C, Q2.C, Q3.C, Q5.C, Q6.C, Q8.C, Part1.GND, Q4.C, R16.Pin_1, R17.Pin_1, R18.Pin_1, R19.Pin_1, R20.Pin_1, R21.Pin_1, R22.Pin_1, Part2.GND, Part3.GND, Part4.GND, Part5.GND, R30.Pin_0, R31.Pin_0
  N4: LED2.cathode, R32.Pin_0
  N5: LED3.cathode, R34.Pin_0
  N6: LED4.cathode, R33.Pin_0
  N7: 7_Segment1.Segment_E, Q4.E
  N8: 7_Segment1.Segment_D, 7_Segment1.Segment_C, Q5.E
  VCC: 7_Segment1.common_anode, 7_Segment2.common_anode, Power_plug1.VCC, Part1.VIN
  N9: 7_Segment1.Segment_DP, Part1.D2_PWM
  N10: 7_Segment1.Segment_B, Q8.E
  N11: 7_Segment1.Segment_A, Q3.E
  N12: 7_Segment1.Segment_F, Q2.E
  N13: 7_Segment1.Segment_G, Q1.E
  N14: 7_Segment2.Segment_E, Q14.E
  N15: 7_Segment2.Segment_D, Q15.E
  N16: 7_Segment2.Segment_C, Q12.E
  N17: 7_Segment2.Segment_DP, Part1.D3_PWM
  N18: 7_Segment2.Segment_B, Q13.E
  N19: 7_Segment2.Segment_A, Q10.E
  N20: 7_Segment2.Segment_F, Q11.E
  N21: 7_Segment2.Segment_G, Q9.E
  N22: Q1.B, R9.Pin_0
  N23: Q2.B, R10.Pin_0
  N24: Q3.B, R11.Pin_0
  N25: Q5.B, R14.Pin_0
  N26: Q6.B, R15.Pin_0
  N27: Q8.B, R12.Pin_0
  N28: Part1.D22, R24.Pin_1
  N29: Part1.D23, R15.Pin_1
  N30: Part1.D24, R25.Pin_1
  N31: Part1.D25, R14.Pin_1
  N32: Part1.D26, R27.Pin_1
  N33: Part1.D27, R13.Pin_1
  N34: Part1.D28, R28.Pin_1
  N35: Part1.D29, R12.Pin_1
  N36: Part1.D30, R29.Pin_1
  N37: Part1.D31, R11.Pin_1
  N38: Part1.D32, R23.Pin_1
  N39: Part1.D33, R10.Pin_1
  N40: Part1.D34, R26.Pin_1
  N41: Part1.D35, R9.Pin_1
  N42: Part1.D38, R32.Pin_1
  N43: Part1.D39, R35.Pin_1
  N44: Part1.D40, R34.Pin_1
  N45: Part1.D41, R33.Pin_1
  N46: Part1.D42, Part4.RST
  N47: Part1.D43, Part4.SDA
  N48: Part1.D44, Part5.RST
  N49: Part1.D45, Part5.SDA
  N50: Part1.D46, Part2.RST
  N51: Part1.D47, Part2.SDA
  N52: Part1.D48, Part3.RST
  N53: Part1.D49, Part3.SDA
  N54: Part1.D50, Part2.MISO, Part3.MISO, Part4.MISO, Part5.MISO
  N55: Part1.D51, Part2.MOSI, Part3.MOSI, Part4.MOSI, Part5.MOSI
  N56: Part1.D52, Part2.SCK, Part3.SCK, Part4.SCK, Part5.SCK
  N57: Q4.B, R13.Pin_0
  N58: Q9.B, R26.Pin_0
  N59: Q9.C, R19.Pin_0
  N60: Q10.B, R29.Pin_0
  N61: Q10.C, R21.Pin_0
  N62: Q11.B, R23.Pin_0
  N63: Q11.C, R20.Pin_0
  N64: Q12.B, R24.Pin_0
  N65: Q12.C, R22.Pin_0
  N66: Q13.B, R28.Pin_0
  N67: Q13.C, R18.Pin_0
  N68: Q14.B, R27.Pin_0
  N69: Q14.C, R17.Pin_0
  N70: Q15.B, R25.Pin_0
  N71: Q15.C, R16.Pin_0

custom parts:
  RFID-RC522-v3: A simple China made RFID-RC522 Reader (6x4 cm); do check the pin labels, as this is a MFRC522 based clone.
